# Fritzing sketch scheme (saved by Fritzing 0.9.3b)

parts:
  WeMos_D1_Mini1 = WeMos D1 Mini
  S1 = Toggle Switch [package=THT]
  LED2 = LED - 5mm [color="Red (633nm)" current=0.030 package="5 mm [THT]"]  # not connected
  R7 = Resistor [tolerance=±5% resistance=3.3k power=0.25 package=THT]
  R8 = Temperature Sensor (Thermistor) [thermistor_type=NTC part_number=MF52 package=THT]
  W5500_Module1 = W5500 Ethernet module [package="DIP (Dual Inline) [THT]"]
  LED6 = LED - 5mm [color="Red (633nm)" current=0.030 package="5 mm [THT]"]  # not connected
  LED7 = LED - 5mm [color="Red (633nm)" current=0.030 package="5 mm [THT]"]  # not connected
  LED8 = LED - 5mm [color="Red (633nm)" current=0.030 package="5 mm [THT]"]  # not connected
  LED9 = LED - 5mm [color="Red (633nm)" current=0.030 package="5 mm [THT]"]  # not connected
  LED10 = LED - 5mm [color="Red (633nm)" current=0.030 package="5 mm [THT]"]  # not connected
  LED11 = LED - 5mm [color="Red (633nm)" current=0.030 package="5 mm [THT]"]  # not connected
  LED12 = LED - 5mm [color="Red (633nm)" current=0.030 package="5 mm [THT]"]  # not connected
  LED13 = LED - 5mm [color="Red (633nm)" current=0.030 package="5 mm [THT]"]  # not connected
  LED14 = LED - 5mm [color="Red (633nm)" current=0.030 package="5 mm [THT]"]  # not connected
  LED15 = LED - 5mm [color="Red (633nm)" current=0.030 package="5 mm [THT]"]  # not connected
  LED16 = LED - 5mm [color="Red (633nm)" current=0.030 package="5 mm [THT]"]  # not connected
  LED17 = LED - 5mm [color="Red (633nm)" current=0.030 package="5 mm [THT]"]  # not connected
  LED18 = LED - 5mm [color="Red (633nm)" current=0.030 package="5 mm [THT]"]  # not connected
  LED19 = LED - 5mm [color="Red (633nm)" current=0.030 package="5 mm [THT]"]  # not connected
  LED20 = LED - 5mm [color="Red (633nm)" current=0.030 package="5 mm [THT]"]  # not connected
  Часть1 = Adafruit PCF8575 [part_number="Adafruit #5611"]
  R9 = 10k Ω Resistor [package=THT]
  R10 = 10k Ω Resistor [package=THT]
  R11 = 10k Ω Resistor [package=THT]
  R12 = 10k Ω Resistor [package=THT]
  R13 = 10k Ω Resistor [package=THT]
  R14 = 10k Ω Resistor [package=THT]
  R15 = 10k Ω Resistor [package=THT]
  R16 = 10k Ω Resistor [package=THT]
  R17 = 10k Ω Resistor [package=THT]
  R18 = 10k Ω Resistor [package=THT]
  R19 = 10k Ω Resistor [package=THT]
  R20 = 10k Ω Resistor [package=THT]
  R21 = 10k Ω Resistor [package=THT]
  R22 = 10k Ω Resistor [package=THT]
  R23 = 10k Ω Resistor [package=THT]
  R24 = 10k Ω Resistor [package=THT]
  R25 = Resistor [tolerance=±5% resistance=4.7k power=0.25 package=THT]

nets:
  N1: WeMos_D1_Mini1.3V3, R7.Pin_0
  N2: WeMos_D1_Mini1.A0, R7.Pin_1, R8.pin_0
  N3: WeMos_D1_Mini1.D1, Часть1.SCL
  N4: WeMos_D1_Mini1.D2, Часть1.SDA
  N5: WeMos_D1_Mini1.D3, S1.L1
  N6: WeMos_D1_Mini1.D5, W5500_Module1.SCLK
  N7: WeMos_D1_Mini1.D6, W5500_Module1.MISO
  N8: WeMos_D1_Mini1.D7, W5500_Module1.MOSI
  N9: WeMos_D1_Mini1.D8, W5500_Module1.SCS, R25.Pin_1
  N10: Часть1.GPA0, R17.Pin_1
  N11: Часть1.GPA1, R16.Pin_1
  N12: Часть1.GPA2, R21.Pin_1
  N13: Часть1.GPA3, R22.Pin_1
  N14: Часть1.GPA4, R20.Pin_1
  N15: Часть1.GPA5, R23.Pin_1
  N16: Часть1.GPA6, R19.Pin_1
  N17: Часть1.GPA7, R24.Pin_1
  N18: Часть1.GPB0, R18.Pin_1
  N19: Часть1.GPB1, R15.Pin_1
  N20: Часть1.GPB2, R14.Pin_1
  N21: Часть1.GPB3, R13.Pin_1
  N22: Часть1.GPB4, R12.Pin_1
  N23: Часть1.GPB5, R11.Pin_1
  N24: Часть1.GPB6, R10.Pin_1
  N25: Часть1.GPB7, R9.Pin_1

custom parts:
  WeMos D1 Mini: The D1 mini is a mini wifi board based on ESP-8266EX.
  W5500 Ethernet module: W5500 based SPI Ethernet module for Arduino, etc.
  Adafruit PCF8575: Expand your project possibilities, with the Adafruit PCF8575 GPIO Expander Breakout - an affordable 16 channel I2C expander. GPIO expanders work like this: you have a board with some number of GPIO but not enough for your project - maybe you need more buttons or LEDs. You could upgrade to a board with massive number of GPIO like the Grand Central, or you could pop on one of these boards.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
  10k Ω Resistor: A generic resistor (0.25W)
