# Fritzing sketch АГЕНТ eth (saved by Fritzing 0.9.3b)

parts:
  WeMos_D1_Mini1 = WeMos D1 Mini
  R2 = Resistor [tolerance=±5% power=0.25 resistance=220 package=THT]
  R3 = Resistor [tolerance=±5% power=0.25 resistance=220 package=THT]
  R4 = Resistor [tolerance=±5% power=0.25 resistance=220 package=THT]
  R5 = Resistor [tolerance=±5% power=0.25 resistance=220 package=THT]
  R6 = Resistor [tolerance=±5% power=0.25 resistance=220 package=THT]
  S1 = Toggle Switch [package=THT]
  LED1 = LED - 5mm [color="Red (633nm)" current=0.030 package="5 mm [THT]"]  # not connected
  LED2 = LED - 5mm [color="Red (633nm)" current=0.030 package="5 mm [THT]"]  # not connected
  LED3 = LED - 5mm [color="Red (633nm)" current=0.030 package="5 mm [THT]"]  # not connected
  LED4 = LED - 5mm [color="Red (633nm)" current=0.030 package="5 mm [THT]"]  # not connected
  LED5 = LED - 5mm [color="Red (633nm)" current=0.030 package="5 mm [THT]"]  # not connected
  R7 = Resistor [tolerance=±5% resistance=220 power=0.25 package=THT]
  R8 = Temperature Sensor (Thermistor) [thermistor_type=NTC package=THT]
  W5500_Module1 = W5500 Ethernet module [package="DIP (Dual Inline) [THT]"]

nets:
  N1: WeMos_D1_Mini1.3V3, R7.Pin_0
  N2: WeMos_D1_Mini1.A0, R7.Pin_1, R8.pin_0
  N3: WeMos_D1_Mini1.D1, R6.Pin_0
  N4: WeMos_D1_Mini1.D2, R5.Pin_0
  N5: WeMos_D1_Mini1.D3, S1.L1
  N6: WeMos_D1_Mini1.D4, R3.Pin_0
  N7: WeMos_D1_Mini1.D5, W5500_Module1.SCLK
  N8: WeMos_D1_Mini1.D6, W5500_Module1.MISO
  N9: WeMos_D1_Mini1.D7, W5500_Module1.MOSI
  N10: WeMos_D1_Mini1.D8, W5500_Module1.SCS
  N11: WeMos_D1_Mini1.RX, R4.Pin_0
  N12: WeMos_D1_Mini1.TX, R2.Pin_0

custom parts:
  WeMos D1 Mini: The D1 mini is a mini wifi board based on ESP-8266EX.
  W5500 Ethernet module: W5500 based SPI Ethernet module for Arduino, etc.
